// Logisim project ALU.circ as structural Verilog: 4 circuits, main circuit Resultat
module Resultat (
  input  [3:0] in_1,
  input  in_2,
  input  [4:0] in_3,
  input  [31:0] in_4,
  input  [31:0] in_5,
  output [31:0] S,
  output [3:0] Flags
);

  // Probe on in_1
  ALU alu_1 (.Codop(in_1), .A(in_4), .Shift(in_3), .CarryIn(in_2), .B(in_5), .S(S), .Flags(Flags));
endmodule

module Operations (
  input  [4:0] Shift,
  input  CarryIn,
  input  [31:0] A,
  input  [31:0] B,
  output [31:0] ORR,
  output [31:0] TST,
  output [31:0] MUL,
  output [31:0] EOR,
  output [31:0] MULCout,
  output [31:0] LSL,
  output [31:0] lAND,
  output [31:0] ADC,
  output ADCCout,
  output [31:0] ASR,
  output [31:0] LSR,
  output [31:0] BIC,
  output [31:0] RSB,
  output [31:0] lROR,
  output [31:0] CMP,
  output [31:0] MVN,
  output CMPCout,
  output [31:0] SBC,
  output [31:0] CMN,
  output CMNCout,
  output SBCOut,
  output CMNV
);

  wire ANeg, APos, BNeg, BPos, comparator_1_gt, comparator_1_lt, negator_2_out;

  Subtractor #(.width(32)) subtractor_1 (.a(A), .b(B), .out(CMP), .bout(CMPCout));  // open: bin
  assign EOR = A ^ B;  // XOR_Gate xor_1, 32 bits wide
  Shifter #(.width(32)) shifter_1 (.in(B), .\dist (Shift), .out(LSL));
  Shifter #(.width(32), .shift("ar")) shifter_2 (.in(B), .\dist (Shift), .out(ASR));
  Negator #(.width(32)) negator_1 (.in(B), .out(RSB));
  Adder #(.width(32)) adder_1 (.a(A), .b(B), .out(CMN), .cout(CMNCout));  // open: cin
  Comparator #(.width(32)) comparator_1 (
    .a(CMN), .b({32{1'b0}}), .gt(comparator_1_gt), .lt(comparator_1_lt));  // open: eq
  and and_1 (CMNV, ANeg, BNeg, comparator_1_gt);
  and and_2 (CMNV, comparator_1_lt, APos, BPos);
  assign lAND = A & B;  // AND_Gate and_3, 32 bits wide
  assign MVN = ~B;  // NOT_Gate not_1, 32 bits wide
  assign ORR = A | B;  // OR_Gate or_1, 32 bits wide
  Multiplier #(.width(32)) multiplier_1 (.a(A), .b(B), .out(MUL), .cout(MULCout));  // open: cin
  assign BIC = A & MVN;  // AND_Gate and_4, 32 bits wide
  Negator #(.width(1)) negator_2 (.in(CarryIn), .out(negator_2_out));
  Subtractor #(.width(32)) subtractor_2 (.a(A), .b(B), .out(SBC), .bin(negator_2_out), .bout(SBCOut));
  Adder #(.width(32)) adder_2 (.a(A), .b(B), .out(ADC), .cin(CarryIn), .cout(ADCCout));
  Comparator #(.width(32)) comparator_2 (.a(A), .b({32{1'b0}}), .gt(APos), .lt(ANeg));  // open: eq
  Comparator #(.width(32)) comparator_3 (.a(B), .b({32{1'b0}}), .gt(BPos), .lt(BNeg));  // open: eq
  Shifter #(.width(32), .shift("ar")) shifter_3 (.in(B), .\dist (Shift), .out(LSR));
  Shifter #(.width(32), .shift("rr")) shifter_4 (.in(B), .\dist (Shift), .out(lROR));

  assign TST = EOR;

  // Other names for the same wires on the sheet: Cin = CarryIn
endmodule

module ALU (
  input  [3:0] Codop,
  input  [31:0] A,
  input  [4:0] Shift,
  input  CarryIn,
  input  [31:0] B,
  output [31:0] S,
  output [3:0] Flags
);

  wire ADCCout, and_1_out, and_2_out, bitselector_1_out, bitselector_3_out, bitselector_4_out,
       bitselector_5_out, bitselector_6_out, CMNCout, CMPCout, SBCout, subtractor_1_bout, undriven,
       xnor_1_out, xor_1_out, xor_2_out, xor_3_out;
  wire [4:0] negator_1_out, subtractor_1_out;
  wire [31:0] ADC, ASR, BIC, CMN, CMP, EOR, lAND, lROR, LSL, LSR, MUL, MULCout, MVN, ORR, RSB, SBC, TST;

  Multiplexer #(.select(4), .width(32), .enable("false")) multiplexer_1 (
    .in0(lAND), .in1(EOR), .in2(LSL), .in3(LSR), .in4(ASR), .in5(ADC), .in6(SBC), .in7(lROR), .in8(TST),
    .in9(RSB), .in10(CMP), .in11(CMN), .in12(ORR), .in13(MUL), .in14(BIC), .in15(MVN), .out(S), .sel(Codop));
  Comparator #(.width(32)) comparator_1 (.a(S), .b({32{1'b0}}), .eq(Flags[1]), .lt(Flags[0]));  // open: gt
  Operations operations_1 (
    .Shift(Shift), .CarryIn(CarryIn), .A(A), .B(B), .ORR(ORR), .TST(TST), .MUL(MUL), .EOR(EOR),
    .MULCout(MULCout), .LSL(LSL), .lAND(lAND), .ADC(ADC), .ADCCout(ADCCout), .ASR(ASR), .LSR(LSR), .BIC(BIC),
    .RSB(RSB), .lROR(lROR), .CMP(CMP), .MVN(MVN), .CMPCout(CMPCout), .SBC(SBC), .CMN(CMN), .CMNCout(CMNCout),
    .SBCOut(SBCout));  // open: CMNV
  Negator #(.width(5)) negator_1 (.in(Shift), .out(negator_1_out));
  Subtractor #(.width(5)) subtractor_1 (
    .a(Shift), .b(5'b00001), .out(subtractor_1_out), .bout(subtractor_1_bout));  // open: bin
  BitSelector #(.width(32)) bitselector_1 (.in(A), .out(bitselector_1_out), .sel({5{1'b1}}));
  BitSelector #(.width(32)) bitselector_2 (.in(A), .out(bitselector_1_out), .sel({5{1'b1}}));
  BitSelector #(.width(32)) bitselector_3 (.in(B), .out(bitselector_3_out), .sel({5{1'b1}}));
  BitSelector #(.width(32)) bitselector_4 (.in(S), .out(bitselector_4_out), .sel({5{1'b1}}));
  BitSelector #(.width(32)) bitselector_5 (.in(B), .out(bitselector_5_out), .sel(negator_1_out));
  BitSelector #(.width(32)) bitselector_6 (.in(B), .out(bitselector_6_out), .sel(subtractor_1_out));
  xnor xnor_1 (xnor_1_out, bitselector_1_out, bitselector_3_out);
  xor xor_1 (xor_1_out, bitselector_1_out, bitselector_3_out);
  xor xor_2 (xor_2_out, bitselector_1_out, bitselector_4_out);
  xor xor_3 (xor_3_out, bitselector_1_out, bitselector_4_out);
  Multiplexer #(.select(4), .enable("false")) multiplexer_2 (
    .in0(1'b0), .in1(1'b0), .in2(bitselector_5_out), .in3(bitselector_6_out), .in4(bitselector_6_out),
    .in5(ADCCout), .in6(SBCout), .in7(undriven), .in8(1'b0), .in9(1'b1), .in10(CMPCout), .in11(CMNCout),
    .in12(1'b0), .in13(1'b0), .in14(1'b0), .in15(1'b0), .out(Flags[2]), .sel(Codop));
  and and_1 (and_1_out, xnor_1_out, xor_3_out);
  and and_2 (and_2_out, xor_1_out, xor_2_out);
  Multiplexer #(.select(4), .enable("false")) multiplexer_3 (
    .in0(1'b0), .in1(1'b0), .in2(1'b0), .in3(1'b0), .in4(1'b0), .in5(and_1_out), .in6(and_2_out), .in7(1'b0),
    .in8(1'b0), .in9(1'b0), .in10(and_2_out), .in11(and_1_out), .in12(1'b0), .in13(1'b0), .in14(1'b0),
    .in15(1'b0), .out(Flags[3]), .sel(Codop));

  // Other names for the same wires on the sheet: N = Flags[0]; Z = Flags[1]; C = Flags[2]; V = Flags[3]

  // Notes on the sheet:
  //   Note: for ROR, C = N
  //   Note 2: assume that shift > 0 for LSL and LSR
endmodule

module tmp (
);

  wire and_1_out, and_2_out, and_3_out, and_4_out, bitselector_1_out, bitselector_2_out, bitselector_3_out,
       bitselector_5_out, bitselector_6_out, bitselector_7_out, not_1_out, V, xnor_1_out, xor_1_out,
       xor_2_out, xor_3_out, xor_4_out, xor_5_out;
  wire [3:0] Codop;
  wire [31:0] A, B, S;

  BitSelector #(.width(32)) bitselector_1 (.in(B), .out(bitselector_1_out), .sel({5{1'b1}}));
  BitSelector #(.width(32)) bitselector_2 (.in(S), .out(bitselector_2_out), .sel({5{1'b1}}));
  BitSelector #(.width(32)) bitselector_3 (.in(A), .out(bitselector_3_out), .sel({5{1'b1}}));
  BitSelector #(.width(32)) bitselector_4 (.in(A), .out(bitselector_3_out), .sel({5{1'b1}}));
  BitSelector #(.width(32)) bitselector_5 (.in(B), .out(bitselector_5_out), .sel({5{1'b1}}));
  BitSelector #(.width(32)) bitselector_6 (.in(S), .out(bitselector_6_out), .sel({5{1'b1}}));
  BitSelector #(.width(32)) bitselector_7 (.in(A), .out(bitselector_7_out), .sel({5{1'b1}}));
  BitSelector #(.width(32)) bitselector_8 (.in(A), .out(bitselector_7_out), .sel({5{1'b1}}));
  xor xor_1 (xor_1_out, bitselector_7_out, bitselector_1_out);
  xor xor_2 (xor_2_out, bitselector_1_out, bitselector_2_out);
  xnor xnor_1 (xnor_1_out, bitselector_3_out, bitselector_5_out);
  xor xor_3 (xor_3_out, bitselector_3_out, bitselector_5_out);
  xor xor_4 (xor_4_out, bitselector_3_out, bitselector_6_out);
  not not_1 (not_1_out, xor_2_out);
  xor xor_5 (xor_5_out, bitselector_3_out, bitselector_6_out);
  and and_1 (and_1_out, xor_1_out, not_1_out);
  and and_2 (and_2_out, xor_1_out, xor_2_out);
  and and_3 (and_3_out, xnor_1_out, xor_5_out);
  and and_4 (and_4_out, xor_3_out, xor_4_out);
  Multiplexer #(.select(4), .enable("false")) multiplexer_1 (
    .in0(1'b0), .in1(1'b0), .in2(1'b0), .in3(1'b0), .in4(1'b0), .in5(and_1_out), .in6(and_2_out), .in7(1'b0),
    .in8(1'b0), .in9(1'b0), .in10(and_2_out), .in11(and_1_out), .in12(1'b0), .in13(1'b0), .in14(1'b0),
    .in15(1'b0), .out(V), .sel(Codop));
  Multiplexer #(.select(4), .enable("false")) multiplexer_2 (
    .in0(1'b0), .in1(1'b0), .in2(1'b0), .in3(1'b0), .in4(1'b0), .in5(and_3_out), .in6(and_4_out), .in7(1'b0),
    .in8(1'b0), .in9(1'b0), .in10(and_4_out), .in11(and_3_out), .in12(1'b0), .in13(1'b0), .in14(1'b0),
    .in15(1'b0), .out(V), .sel(Codop));
endmodule
