// Logisim project ARM.circ as structural Verilog: 1 circuit, main circuit main
module main (
);

  // Resultat resultat_1: pin names not known
  // BancRegistre bancregistre_1: pin names not known
endmodule
