// Logisim project BancDeRegistres.circ as structural Verilog: 1 circuit, main circuit BancRegistre
module BancRegistre (
  input  [31:0] DataIn,
  input  [2:0] RegA,
  input  Clk,
  input  Reset,
  input  [2:0] RegDest,
  input  [2:0] RegB,
  output [31:0] AOut,
  output [31:0] R0,
  output [31:0] R1,
  output [31:0] R2,
  output [31:0] R3,
  output [31:0] R4,
  output [31:0] R5,
  output [31:0] R6,
  output [31:0] R7,
  output [31:0] BOut
);

  wire demultiplexer_1_out0, demultiplexer_1_out1, demultiplexer_1_out2, demultiplexer_1_out3,
       demultiplexer_1_out4, demultiplexer_1_out5, demultiplexer_1_out6, demultiplexer_1_out7;
  wire [31:0] register_1_q, register_2_q, register_3_q, register_4_q, register_5_q, register_6_q,
       register_7_q, register_8_q;

  Demultiplexer #(.select(3), .enable("false")) demultiplexer_1 (
    .out0(demultiplexer_1_out0), .out1(demultiplexer_1_out1), .out2(demultiplexer_1_out2),
    .out3(demultiplexer_1_out3), .out4(demultiplexer_1_out4), .out5(demultiplexer_1_out5),
    .out6(demultiplexer_1_out6), .out7(demultiplexer_1_out7), .sel(RegDest));  // open: in
  Register #(.width(32)) register_1 (.D(DataIn), .en(demultiplexer_1_out0), .clk(Clk), .Q(register_1_q), .clr(Reset));
  Register #(.width(32)) register_2 (.D(DataIn), .en(demultiplexer_1_out1), .clk(Clk), .Q(register_2_q), .clr(Reset));
  Register #(.width(32)) register_3 (.D(DataIn), .en(demultiplexer_1_out2), .clk(Clk), .Q(register_3_q), .clr(Reset));
  Register #(.width(32)) register_4 (.D(DataIn), .en(demultiplexer_1_out3), .clk(Clk), .Q(register_4_q));  // open: clr
  Register #(.width(32)) register_5 (.D(DataIn), .en(demultiplexer_1_out4), .clk(Clk), .Q(register_5_q), .clr(Reset));
  Register #(.width(32)) register_6 (.D(DataIn), .en(demultiplexer_1_out5), .clk(Clk), .Q(register_6_q), .clr(Reset));
  Register #(.width(32)) register_7 (.D(DataIn), .en(demultiplexer_1_out6), .clk(Clk), .Q(register_7_q), .clr(Reset));
  Register #(.width(32)) register_8 (.D(DataIn), .en(demultiplexer_1_out7), .clk(Clk), .Q(register_8_q), .clr(Reset));
  Multiplexer #(.select(3), .width(32), .enable("false")) multiplexer_1 (
    .in0(register_1_q), .in1(register_2_q), .in2(register_3_q), .in3(register_4_q), .in4(register_5_q),
    .in5(register_6_q), .in6(register_7_q), .in7(register_8_q), .out(AOut), .sel(RegA));
  Multiplexer #(.select(3), .width(32), .enable("false")) multiplexer_2 (
    .in0(register_1_q), .in1(register_2_q), .in2(register_3_q), .in3(register_4_q), .in4(register_5_q),
    .in5(register_6_q), .in6(register_7_q), .in7(register_8_q), .out(BOut), .sel(RegB));
endmodule
