// Logisim project Controller.circ as structural Verilog: 8 circuits, main circuit Controller
module Controller (
  input  [15:0] Inst,
  input  [3:0] Flags,
  input  Clk,
  input  Reset,
  output Carry,
  output DP_Shift,
  output Imm32_Enable,
  output [4:0] Imm5,
  output [31:0] Imm32,
  output [3:0] ALU_Opcode,
  output [2:0] Rm,
  output [2:0] Rn,
  output [2:0] Rd,
  output [31:0] RAM_Addr,
  output Load,
  output Store,
  output [7:0] PC
);

  wire Conditional_1_verified, Load_Store_1_pc_hold, not_1_out, Opcode_Decoder_1_conditional,
       Opcode_Decoder_1_data_processing, Opcode_Decoder_1_load_store, Opcode_Decoder_1_shift,
       Opcode_Decoder_1_sp_address, Shift_Add_Sub_Mov_1_carry, SP_Address_1_write_enable;
  wire [2:0] Data_Processing_1_rd, Data_Processing_1_rm, Data_Processing_1_rn, Load_Store_1_rd,
       Load_Store_1_rm, Shift_Add_Sub_Mov_1_rd, Shift_Add_Sub_Mov_1_rm, Shift_Add_Sub_Mov_1_rn;
  wire [3:0] Data_Processing_1_alu_opcode, Data_Processing_1_flags_update_mask, flags_apsr_1_flags_out,
       or_1_out, Shift_Add_Sub_Mov_1_alu_opcode, Shift_Add_Sub_Mov_1_flags_update_mask;
  wire [7:0] adder_1_out, adder_2_out, Conditional_1_offset;
  wire [31:0] SP_Address_1_new_stack_pointer, Stack_Pointer_q;

  Register #(.width(32)) Stack_Pointer (
    .D(SP_Address_1_new_stack_pointer), .en(SP_Address_1_write_enable), .clk(Clk), .Q(Stack_Pointer_q),
    .clr(Reset));
  Opcode_Decoder Opcode_Decoder_1 (
    .Opcode(Inst[15:10]), .Shift(Opcode_Decoder_1_shift), .Data_Processing(Opcode_Decoder_1_data_processing),
    .SP_Address(Opcode_Decoder_1_sp_address), .Conditional(Opcode_Decoder_1_conditional),
    .Load_Store(Opcode_Decoder_1_load_store));
  assign or_1_out = Data_Processing_1_flags_update_mask | Shift_Add_Sub_Mov_1_flags_update_mask;  // OR_Gate or_1, 4 bits wide
  Shift_Add_Sub_Mov Shift_Add_Sub_Mov_1 (
    .Imm32_Enable(Imm32_Enable), .Instruction(Inst), .ALU_Opcode(Shift_Add_Sub_Mov_1_alu_opcode),
    .Enable(Opcode_Decoder_1_shift), .Carry(Shift_Add_Sub_Mov_1_carry),
    .Flags_Update_Mask(Shift_Add_Sub_Mov_1_flags_update_mask), .Rd(Shift_Add_Sub_Mov_1_rd),
    .Rm(Shift_Add_Sub_Mov_1_rm), .Imm32(Imm32), .Imm5(Imm5), .Rn(Shift_Add_Sub_Mov_1_rn));  // open: imm3, imm8
  Data_Processing Data_Processing_1 (
    .Rd(Data_Processing_1_rd), .in_1(Inst), .Rn(Data_Processing_1_rn), .Rm(Data_Processing_1_rm),
    .Flags_Update_Mask(Data_Processing_1_flags_update_mask), .in_2(Opcode_Decoder_1_data_processing),
    .ALU_Opcode(Data_Processing_1_alu_opcode));
  Flags_APSR flags_apsr_1 (
    .Update_Mask(or_1_out), .Flags_In(Flags), .Clk(Clk), .Rst(Reset), .Flags_Out(flags_apsr_1_flags_out));
  Load_Store Load_Store_1 (
    .Instruction(Inst), .Load(Load), .RAM_Addr(RAM_Addr), .Store(Store), .Stack_Pointer(Stack_Pointer_q),
    .Enable(Opcode_Decoder_1_load_store), .Rd(Load_Store_1_rd), .Clk(Clk), .Reset(Reset),
    .PC_Hold(Load_Store_1_pc_hold), .Rm(Load_Store_1_rm));
  Conditional Conditional_1 (
    .Offset(Conditional_1_offset), .Instruction(Inst), .Enable(Opcode_Decoder_1_conditional),
    .Verified(Conditional_1_verified), .Z(flags_apsr_1_flags_out[2]), .V(flags_apsr_1_flags_out[0]),
    .N(flags_apsr_1_flags_out[3]), .C(flags_apsr_1_flags_out[1]));
  SP_Address SP_Address_1 (
    .New_Stack_Pointer(SP_Address_1_new_stack_pointer), .Write_Enable(SP_Address_1_write_enable),
    .Stack_Pointer(Stack_Pointer_q), .Instruction(Inst), .Enable(Opcode_Decoder_1_sp_address));
  Adder adder_1 (.a(8'h3), .b(Conditional_1_offset), .out(adder_1_out), .cin(1'b0));  // open: cout
  Adder adder_2 (.a(adder_1_out), .b(PC), .out(adder_2_out), .cin(1'b0));  // open: cout
  and and_1 (DP_Shift, Opcode_Decoder_1_shift, ~Opcode_Decoder_1_data_processing);  // AND_Gate
  not not_1 (not_1_out, Load_Store_1_pc_hold);
  Counter counter_1 (
    .clr(Reset), .load(Conditional_1_verified), .up(1'b1), .count(not_1_out), .clk(Clk), .D(adder_2_out),
    .Q(PC));  // open: carry
  Multiplexer #(.enable("false")) multiplexer_1 (
    .in0(flags_apsr_1_flags_out[1]), .in1(Shift_Add_Sub_Mov_1_carry), .out(Carry), .sel(DP_Shift));
  assign ALU_Opcode = Shift_Add_Sub_Mov_1_alu_opcode | Data_Processing_1_alu_opcode;  // OR_Gate or_2, 4 bits wide
  assign Rm = Shift_Add_Sub_Mov_1_rm | Data_Processing_1_rm | Load_Store_1_rm;  // OR_Gate or_3, 3 bits wide
  assign Rn = Shift_Add_Sub_Mov_1_rn | Data_Processing_1_rn;  // OR_Gate or_4, 3 bits wide
  assign Rd = Shift_Add_Sub_Mov_1_rd | Data_Processing_1_rd | Load_Store_1_rd;  // OR_Gate or_5, 3 bits wide

  // Notes on the sheet:
  //   Extract Opcode
  //   Extract carry
  //   IF Reg_Imm=1 THEN use shift value from register ELSE use shift value from Imm5
  //   Buffer flags for next instruction
  //   Add 3 to offset because ARM pre-increments PC
  //   and does an additionnal prefect operation
endmodule

module Conditional (
  input  Enable,
  input  [15:0] Instruction,
  input  Z,
  input  C,
  input  N,
  input  V,
  output [7:0] Offset,
  output Verified
);

  wire and_1_out, and_2_out, and_3_out, and_4_out, comparator_1_eq, multiplexer_1_out, not_1_out, not_2_out,
       not_3_out, not_4_out, not_5_out;
  wire [7:0] bit_extender_1_out;

  not not_1 (not_1_out, Z);
  not not_2 (not_2_out, C);
  not not_3 (not_3_out, N);
  not not_4 (not_4_out, V);
  and and_1 (and_1_out, C, not_1_out);
  and and_2 (and_2_out, Z, not_2_out);
  Comparator #(.width(1)) comparator_1 (.a(N), .b(V), .eq(comparator_1_eq));  // open: gt, lt
  not not_5 (not_5_out, comparator_1_eq);
  and and_3 (and_3_out, not_1_out, comparator_1_eq);
  and and_4 (and_4_out, Z, not_5_out);
  Multiplexer #(.select(4), .enable("false")) multiplexer_1 (
    .in0(Z), .in1(not_1_out), .in2(C), .in3(not_2_out), .in4(N), .in5(not_3_out), .in6(V), .in7(not_4_out),
    .in8(and_1_out), .in9(and_2_out), .in10(comparator_1_eq), .in11(not_5_out), .in12(and_3_out),
    .in13(and_4_out), .in14(1'b1), .in15(1'b0), .out(multiplexer_1_out), .sel(Instruction[11:8]));
  assign bit_extender_1_out = {{7{Enable}}, Enable};  // Bit_Extender bit_extender_1
  assign Offset = bit_extender_1_out & Instruction[7:0];  // AND_Gate and_5, 8 bits wide
  and and_6 (Verified, Enable, multiplexer_1_out);
endmodule

module Opcode_Decoder (
  input  [5:0] Opcode,
  output Shift,
  output Data_Processing,
  output SP_Address,
  output Conditional,
  output Load_Store
);

  wire and_5_out, and_6_out, and_7_out;

  and and_1 (Shift, ~Opcode[5], ~Opcode[4]);  // AND_Gate
  and and_2 (Data_Processing, ~Opcode[5], Opcode[4]);  // AND_Gate
  and and_3 (SP_Address, Opcode[5], ~Opcode[4], Opcode[3], Opcode[2]);  // AND_Gate
  and and_4 (Conditional, Opcode[5], Opcode[4], ~Opcode[3], Opcode[2]);  // AND_Gate
  and and_5 (and_5_out, Opcode[5], ~Opcode[4], ~Opcode[3]);  // AND_Gate
  and and_6 (and_6_out, ~Opcode[5], Opcode[4], Opcode[3]);  // AND_Gate
  and and_7 (and_7_out, ~Opcode[5], Opcode[4], ~Opcode[3], Opcode[2]);  // AND_Gate
  or or_1 (Load_Store, and_5_out, and_6_out, and_7_out);

  // Notes on the sheet:
  //   SP Address
  //   Load/Store
  //   Shift, add, sub, mov
  //   Data Processing
  //   Conditional branch
endmodule

module Data_Processing (
  input  [15:0] in_1,
  input  in_2,
  output [2:0] Rd,
  output [2:0] Rn,
  output [2:0] Rm,
  output [3:0] Flags_Update_Mask,
  output [3:0] ALU_Opcode
);

  wire [3:0] bit_extender_2_out, multiplexer_1_out;
  wire [15:0] bit_extender_1_out;
  wire [15:10] and_1_out;

  assign bit_extender_1_out = {{15{in_2}}, in_2};  // Bit_Extender bit_extender_1
  assign {and_1_out, ALU_Opcode, Rm, Rd} = in_1 & bit_extender_1_out;  // AND_Gate and_1, 16 bits wide
  assign bit_extender_2_out = {{3{in_2}}, in_2};  // Bit_Extender bit_extender_2
  Multiplexer #(.select(4), .width(4), .enable("false")) multiplexer_1 (
    .in0(4'b1110), .in1(4'b1110), .in2(4'b1110), .in3(4'b1110), .in4(4'b1110), .in5(4'b1111), .in6(4'b1111),
    .in7(4'b1110), .in8(4'b1110), .in9(4'b1111), .in10(4'b1111), .in11(4'b1111), .in12(4'b1110),
    .in13(4'b1100), .in14(4'b1110), .in15(4'b1110), .out(multiplexer_1_out), .sel(ALU_Opcode));
  assign Flags_Update_Mask = multiplexer_1_out & bit_extender_2_out;  // AND_Gate and_2, 4 bits wide

  assign Rn = Rd;

  // Other names for the same wires on the sheet: RdRn[2:0] = Rd; Codop[3:0] = ALU_Opcode

  // Notes on the sheet:
  //   Note 2: RSB instruction has Rn as 1st operand.
  //   MUL instruction has Rn as 1st operand and Rdm as 2nd operand
  //   For simplification purposes, Rm is used for 1st operand both here and in the ALU.
  //   Pull output low on Enable = 0
  //   Note: instructions that does not save the result will still have the second operand as the destination register, the ALU will copy the second register to the destination register
endmodule

module Shift_Add_Sub_Mov (
  input  [15:0] Instruction,
  input  Enable,
  output [3:0] ALU_Opcode,
  output [3:0] Flags_Update_Mask,
  output Imm32_Enable,
  output Carry,
  output [31:0] Imm32,
  output [2:0] Rd,
  output [2:0] Rm,
  output [2:0] Rn,
  output [4:0] Imm5,
  output [2:0] imm3,
  output [7:0] imm8
);

  wire and_2_out, and_3_out, and_4_out, and_5_out, and_6_out, and_7_out, and_8_out, and_9_out,
       priority_encoder_1_en_out;
  wire [2:0] bit_extender_2_out, multiplexer_1_out, multiplexer_3_out, multiplexer_7_out,
       priority_encoder_1_out;
  wire [3:0] bit_extender_3_out, multiplexer_2_out;
  wire [15:0] and_1_out, bit_extender_1_out;
  wire [31:0] bit_extender_4_out, bit_extender_5_out;

  assign bit_extender_1_out = {{15{Enable}}, Enable};  // Bit_Extender bit_extender_1
  assign bit_extender_2_out = {{2{Enable}}, Enable};  // Bit_Extender bit_extender_2
  assign and_1_out = Instruction & bit_extender_1_out;  // AND_Gate and_1, 16 bits wide
  // Probe on and_1_out[13]
  Multiplexer #(.select(3), .width(3), .enable("false")) multiplexer_1 (
    .in0(and_1_out[2:0]), .in1(and_1_out[2:0]), .in2(and_1_out[2:0]), .in3(and_1_out[2:0]),
    .in4(and_1_out[2:0]), .in5(and_1_out[2:0]), .in6(and_1_out[2:0]), .in7(and_1_out[10:8]),
    .out(multiplexer_1_out), .sel(priority_encoder_1_out));
  and and_2 (and_2_out, ~and_1_out[13], ~and_1_out[12], ~and_1_out[11]);  // AND_Gate
  and and_3 (and_3_out, ~and_1_out[13], ~and_1_out[12], and_1_out[11]);  // AND_Gate
  and and_4 (and_4_out, ~and_1_out[13], and_1_out[12], ~and_1_out[11]);  // AND_Gate
  and and_5 (and_5_out, ~and_1_out[13], and_1_out[12], and_1_out[11], ~and_1_out[10], ~and_1_out[9]);  // AND_Gate
  and and_6 (and_6_out, ~and_1_out[13], and_1_out[12], and_1_out[11], ~and_1_out[10], and_1_out[9]);  // AND_Gate
  and and_7 (and_7_out, ~and_1_out[13], and_1_out[12], and_1_out[11], and_1_out[10], ~and_1_out[9]);  // AND_Gate
  and and_8 (and_8_out, ~and_1_out[13], and_1_out[12], and_1_out[11], and_1_out[10], and_1_out[9]);  // AND_Gate
  and and_9 (and_9_out, and_1_out[13], ~and_1_out[12], ~and_1_out[11]);  // AND_Gate
  // Probe on and_2_out
  // Probe on priority_encoder_1_en_out
  Priority_Encoder priority_encoder_1 (
    .in0(and_2_out), .in1(and_3_out), .in2(and_4_out), .in3(and_5_out), .in4(and_6_out), .in5(and_7_out),
    .in6(and_8_out), .in7(and_9_out), .out(priority_encoder_1_out), .en_in(1'b1),
    .en_out(priority_encoder_1_en_out));  // open: gs
  assign Rd = bit_extender_2_out & multiplexer_1_out;  // AND_Gate and_10, 3 bits wide
  // Probe on priority_encoder_1_out
  assign bit_extender_3_out = {{3{Enable}}, Enable};  // Bit_Extender bit_extender_3
  Multiplexer #(.select(3), .width(4), .enable("false")) multiplexer_2 (
    .in0(4'b0010), .in1(4'b0011), .in2(4'b0100), .in3(4'b0101), .in4(4'b0110), .in5(4'b0101), .in6(4'b0110),
    .in7(4'b1001), .out(multiplexer_2_out), .sel(priority_encoder_1_out));
  assign bit_extender_4_out = {{29{1'b0}}, and_1_out[8:6]};  // Bit_Extender bit_extender_4
  assign bit_extender_5_out = {{24{1'b0}}, and_1_out[7:0]};  // Bit_Extender bit_extender_5
  Multiplexer #(.select(3), .width(3), .enable("false")) multiplexer_3 (
    .in0(and_1_out[5:3]), .in1(and_1_out[5:3]), .in2(and_1_out[5:3]), .in3(and_1_out[8:6]),
    .in4(and_1_out[8:6]), .in5(3'b000), .in6(3'b000), .in7(3'b000), .out(multiplexer_3_out),
    .sel(priority_encoder_1_out));
  assign ALU_Opcode = bit_extender_3_out & multiplexer_2_out;  // AND_Gate and_11, 4 bits wide
  Multiplexer #(.select(3), .width(4), .enable("false")) multiplexer_4 (
    .in0(4'b1110), .in1(4'b1110), .in2(4'b1110), .in3(4'b1111), .in4(4'b1111), .in5(4'b1111), .in6(4'b1111),
    .in7(4'b1100), .out(Flags_Update_Mask), .sel(priority_encoder_1_out));
  Multiplexer #(.select(3), .enable("false")) multiplexer_5 (
    .in0(1'b0), .in1(1'b0), .in2(1'b0), .in3(1'b0), .in4(1'b1), .in5(1'b0), .in6(1'b1), .in7(1'b0),
    .out(Carry), .sel(priority_encoder_1_out));
  Multiplexer #(.select(3), .width(32), .enable("false")) multiplexer_6 (
    .in0({32{1'b0}}), .in1({32{1'b0}}), .in2({32{1'b0}}), .in3({32{1'b0}}), .in4({32{1'b0}}),
    .in5(bit_extender_4_out), .in6(bit_extender_4_out), .in7(bit_extender_5_out), .out(Imm32),
    .sel(priority_encoder_1_out));
  Multiplexer #(.select(3), .width(3), .enable("false")) multiplexer_7 (
    .in0(3'b000), .in1(3'b000), .in2(3'b000), .in3(and_1_out[5:3]), .in4(and_1_out[5:3]),
    .in5(and_1_out[5:3]), .in6(and_1_out[5:3]), .in7(3'b000), .out(multiplexer_7_out),
    .sel(priority_encoder_1_out));
  Multiplexer #(.select(3), .width(5), .enable("false")) multiplexer_8 (
    .in0(and_1_out[10:6]), .in1(and_1_out[10:6]), .in2(and_1_out[10:6]), .in3({5{1'b0}}), .in4({5{1'b0}}),
    .in5({5{1'b0}}), .in6({5{1'b0}}), .in7({5{1'b0}}), .out(Imm5), .sel(priority_encoder_1_out));
  Multiplexer #(.select(3), .width(3), .enable("false")) multiplexer_9 (
    .in0(3'b000), .in1(3'b000), .in2(3'b000), .in3(and_1_out[8:6]), .in4(and_1_out[8:6]), .in5(3'b000),
    .in6(3'b000), .in7(3'b000), .out(imm3), .sel(priority_encoder_1_out));
  Multiplexer #(.select(3), .width(8), .enable("false")) multiplexer_10 (
    .in0({8{1'b0}}), .in1({8{1'b0}}), .in2({8{1'b0}}), .in3({8{1'b0}}), .in4({8{1'b0}}), .in5({8{1'b0}}),
    .in6({8{1'b0}}), .in7(and_1_out[7:0]), .out(imm8), .sel(priority_encoder_1_out));
  assign Rm = multiplexer_3_out & bit_extender_2_out;  // AND_Gate and_12, 3 bits wide
  assign Rn = multiplexer_7_out & bit_extender_2_out;  // AND_Gate and_13, 3 bits wide
  Multiplexer #(.select(3), .enable("false")) multiplexer_11 (
    .in0(1'b0), .in1(1'b0), .in2(1'b0), .in3(1'b0), .in4(1'b0), .in5(1'b1), .in6(1'b1), .in7(1'b1),
    .out(Imm32_Enable), .sel(priority_encoder_1_out));

  // Notes on the sheet:
  //   Pull output low on Enable = 0
  //   Note 3: Imm32_Enable forces the use of the immediate for Rm register
  //   Note: ALU uses Rn register for shifts. Use Rn instead of Rm for shifts (immediate) here too
  //   Note 2: MOV uses RSB ALU opcode with Imm8 reversed so that it is copied to output register
  //   LSL
  //   LSR
  //   ASR
  //   ADD(register)
  //   SUB (register)
  //   ADD (immediate)
  //   SUB (immediate)
  //   MOV (immediate)
  //   ALU will use Imm32 instead of Rm
  //   Enable carry for SUB since it is reversed in ALU
endmodule

module Load_Store (
  input  [15:0] Instruction,
  input  Enable,
  input  [31:0] Stack_Pointer,
  input  Clk,
  input  Reset,
  output Store,
  output [2:0] Rm,
  output [2:0] Rd,
  output [31:0] RAM_Addr,
  output Load,
  output PC_Hold
);

  wire and_1_out, Load_t, not_1_out, not_2_out, or_1_out, register_1_q;
  wire [2:0] bit_extender_2_out;
  wire [31:0] adder_1_out, bit_extender_1_out, bit_extender_3_out;

  assign bit_extender_1_out = {{24{Instruction[7]}}, Instruction[7:0]};  // Bit_Extender bit_extender_1
  Adder #(.width(32)) adder_1 (.a(bit_extender_1_out), .b(Stack_Pointer), .out(adder_1_out));  // open: cin, cout
  Register #(.width(1)) register_1 (.D(Load_t), .en(1'b1), .clk(Clk), .Q(register_1_q), .clr(Reset));
  and and_1 (and_1_out, not_1_out, Load_t);
  or or_1 (or_1_out, Load_t, register_1_q);
  // AND_Gate and_2 has open pins: in0=register_1_q, in1=Enable, out=open
  not not_1 (not_1_out, Load);
  Register #(.width(1)) register_2 (.D(and_1_out), .en(1'b1), .clk(Clk), .Q(Load), .clr(Reset));
  not not_2 (not_2_out, Instruction[11]);
  assign bit_extender_2_out = {{2{Enable}}, Enable};  // Bit_Extender bit_extender_2
  assign bit_extender_3_out = {{31{Enable}}, Enable};  // Bit_Extender bit_extender_3
  // AND_Gate and_3 has open pins: in0=or_1_out, in1=Enable, out=open
  and and_4 (Store, not_2_out, Enable);
  and and_5 (Load_t, Instruction[11], Enable);
  assign Rd = Instruction[10:8] & bit_extender_2_out;  // AND_Gate and_6, 3 bits wide
  assign RAM_Addr = bit_extender_3_out & adder_1_out;  // AND_Gate and_7, 32 bits wide

  assign PC_Hold = Load;
  assign Rm = Rd;

  // Notes on the sheet:
  //   Delay load and hold PC for 1 cycle for the RAM to send out requested data 
endmodule

module SP_Address (
  input  Enable,
  input  [15:0] Instruction,
  input  [31:0] Stack_Pointer,
  output Write_Enable,
  output [31:0] New_Stack_Pointer
);

  wire comparator_1_eq, not_1_out;
  wire [31:0] adder_1_out, bit_extender_1_out, subtractor_1_out;

  assign bit_extender_1_out = {{24{Instruction[7]}}, Instruction[7:0]};  // Bit_Extender bit_extender_1
  Adder #(.width(32)) adder_1 (.a(Stack_Pointer), .b(bit_extender_1_out), .out(adder_1_out));  // open: cin, cout
  Subtractor #(.width(32)) subtractor_1 (
    .a(Stack_Pointer), .b(bit_extender_1_out), .out(subtractor_1_out));  // open: bin, bout
  Multiplexer #(.width(32), .enable("false")) multiplexer_1 (
    .in0(adder_1_out), .in1(subtractor_1_out), .out(New_Stack_Pointer), .sel(Instruction[8]));
  Comparator #(.width(32)) comparator_1 (
    .a(New_Stack_Pointer), .b(Stack_Pointer), .eq(comparator_1_eq));  // open: gt, lt
  not not_1 (not_1_out, comparator_1_eq);
  and and_1 (Write_Enable, Enable, not_1_out);

  // Notes on the sheet:
  //   Pull output low on Enable = 0
endmodule

module Flags_APSR (
  input  [3:0] Update_Mask,
  input  [3:0] Flags_In,
  input  Clk,
  input  Rst,
  output [3:0] Flags_Out
);

  wire [3:0] and_1_out, and_2_out, or_1_out;

  assign and_1_out = Flags_Out & ~Update_Mask;  // AND_Gate and_1, 4 bits wide
  assign and_2_out = Update_Mask & Flags_In;  // AND_Gate and_2, 4 bits wide
  assign or_1_out = and_1_out | and_2_out;  // OR_Gate or_1, 4 bits wide
  Register #(.width(4)) register_1 (.D(or_1_out), .en(1'b1), .clk(Clk), .Q(Flags_Out), .clr(Rst));
endmodule
