// Logisim project Machine.circ as structural Verilog: 2 circuits, main circuit main
module main (
  input  GPIO_A1,
  input  GPIO_A3,
  input  GPIO_A5,
  input  GPIO_A7,
  input  GPIO_A9,
  input  GPIO_A11,
  input  GPIO_A13,
  input  GPIO_A15,
  input  GPIO_A17,
  input  GPIO_A19,
  input  GPIO_A21,
  input  GPIO_A23,
  input  GPIO_A25,
  input  GPIO_A27,
  input  GPIO_A29,
  input  GPIO_A31,
  input  GPIO_A33,
  input  GPIO_A35,
  input  GPIO_B1,
  input  GPIO_B3,
  input  GPIO_B5,
  input  GPIO_B7,
  input  GPIO_B9,
  input  GPIO_B11,
  input  GPIO_B13,
  input  GPIO_B15,
  input  GPIO_B17,
  input  GPIO_B19,
  input  GPIO_B21,
  input  GPIO_B23,
  input  GPIO_B25,
  input  GPIO_B27,
  input  GPIO_B29,
  input  GPIO_B31,
  input  GPIO_B33,
  input  GPIO_B35,
  output GPIO_A2,
  output GPIO_A4,
  output GPIO_A6,
  output GPIO_A8,
  output GPIO_A10,
  output GPIO_A12,
  output GPIO_A14,
  output GPIO_A16,
  output GPIO_A18,
  output GPIO_A20,
  output GPIO_A22,
  output GPIO_A24,
  output GPIO_A26,
  output GPIO_A28,
  output GPIO_A30,
  output GPIO_A32,
  output GPIO_A34,
  output GPIO_A36,
  output GPIO_B2,
  output GPIO_B4,
  output GPIO_B6,
  output GPIO_B8,
  output GPIO_B10,
  output GPIO_B12,
  output GPIO_B14,
  output GPIO_B16,
  output GPIO_B18,
  output GPIO_B20,
  output GPIO_B22,
  output GPIO_B24,
  output GPIO_B26,
  output GPIO_B28,
  output GPIO_B30,
  output GPIO_B32,
  output GPIO_B34,
  output GPIO_B36
);

  wire Clk_Button_out, clock_1_out, CPU_1_store, Rst_Button_out;
  wire [7:0] RAM_Addr, ROM_Addr;
  wire [15:0] ROMa_data;
  wire [31:0] CPU_1_r0, CPU_1_r1, CPU_1_r2, CPU_1_r3, CPU_1_r4, CPU_1_r5, CPU_1_r6, CPU_1_r7, CPU_1_ram_out,
       RAMa_dout;
  wire [31:8] CPU_1_ram_addr;

  RAM #(.dataWidth(32), .databus("bibus")) RAMa (
    .addr(RAM_Addr), .we(CPU_1_store), .oe(1'b1), .clk(clock_1_out), .din(CPU_1_ram_out), .dout(RAMa_dout));
  Clock clock_1 (.out(clock_1_out));
  LED A0 (.in(RAMa_dout[0]));
  LED A1 (.in(RAMa_dout[1]));
  LED A2 (.in(RAMa_dout[2]));
  ROM #(.dataWidth(16)) ROMa (.addr(ROM_Addr), .data(ROMa_data));
  Button Clk_Button (.out(Clk_Button_out));
  Button Rst_Button (.out(Rst_Button_out));
  LED A3 (.in(RAMa_dout[3]));
  LED A4 (.in(RAMa_dout[4]));
  LED A5 (.in(RAMa_dout[5]));
  LED A6 (.in(RAMa_dout[6]));
  LED A7 (.in(RAMa_dout[7]));
  LED L0 (.in(CPU_1_r0[0]));
  // Probe on CPU_1_r1
  // Probe on CPU_1_r0
  LED L3 (.in(CPU_1_r0[3]));
  LED L1 (.in(CPU_1_r0[1]));
  LED L2 (.in(CPU_1_r0[2]));
  // Probe on CPU_1_r3
  // Probe on CPU_1_r2
  // Probe on CPU_1_r5
  // Probe on CPU_1_r4
  LED L4 (.in(CPU_1_r0[4]));
  LED L5 (.in(CPU_1_r0[5]));
  // Probe on CPU_1_r7
  // Probe on CPU_1_r6
  CPU CPU_1 (
    .ROM_Addr(ROM_Addr), .RAM_In(RAMa_dout), .R3(CPU_1_r3), .R7(CPU_1_r7), .R2(CPU_1_r2), .R6(CPU_1_r6),
    .RAM_Addr({CPU_1_ram_addr, RAM_Addr}), .R1(CPU_1_r1), .R5(CPU_1_r5), .ROM_In(ROMa_data), .R0(CPU_1_r0),
    .R4(CPU_1_r4), .Clk(clock_1_out), .RAM_Out(CPU_1_ram_out), .Reset(Rst_Button_out), .Store(CPU_1_store));
  LED L6 (.in(CPU_1_r0[6]));
  LED L7 (.in(CPU_1_r0[7]));
  LED LED_1 (.in(RAM_Addr[0]));
  LED LED_2 (.in(RAM_Addr[1]));
  LED LED_3 (.in(RAM_Addr[2]));
  LED LED_4 (.in(RAM_Addr[3]));
  LED LED_5 (.in(RAM_Addr[4]));
  LED LED_6 (.in(RAM_Addr[5]));
  LED LED_7 (.in(RAM_Addr[6]));
  LED LED_8 (.in(RAM_Addr[7]));

  // Notes on the sheet:
  //   contents of ROMa (hex, n*v repeats v):
  //   b08c 2000 9008 21ff 9104 9000 defe 9800 9904 4288 da08 defe 9800 9908 4081 9108 defe 9800 1c40 9000
  //   def0 b00c
  //   Use only 8 bit adresses
  //   VCC 5V
  //   VCC 3.3V
  //   VCC 5V
  //   VCC 3.3V
  //   GROUND
  //   GROUND
  //   GROUND
  //   GROUND
endmodule

module CPU (
  input  [31:0] RAM_In,
  input  [15:0] ROM_In,
  input  Clk,
  input  Reset,
  output [31:0] R3,
  output [31:0] R7,
  output [31:0] R2,
  output [31:0] R1,
  output [31:0] R6,
  output [31:0] R5,
  output [31:0] R0,
  output [31:0] R4,
  output [31:0] RAM_Out,
  output [31:0] RAM_Addr,
  output [7:0] ROM_Addr,
  output Store
);

  wire Controller_1_carry, Controller_1_dp_shift, Controller_1_imm32_enable, Controller_1_load;
  wire [2:0] Controller_1_rd, Controller_1_rm, Controller_1_rn;
  wire [3:0] Controller_1_alu_opcode, resultat_1_flags;
  wire [4:0] and_2_out, and_3_out, bit_extender_2_out, Controller_1_imm5, or_1_out;
  wire [31:0] and_1_out, and_4_out, AOut, bit_extender_1_out, bit_extender_3_out, bit_extender_4_out,
       Controller_1_imm32, or_2_out, Regs_1_bout, resultat_1_s;

  Controller Controller_1 (
    .Imm5(Controller_1_imm5), .Imm32(Controller_1_imm32), .Rn(Controller_1_rn), .Inst(ROM_In),
    .ALU_Opcode(Controller_1_alu_opcode), .Rd(Controller_1_rd), .Flags(resultat_1_flags),
    .Rm(Controller_1_rm), .Imm32_Enable(Controller_1_imm32_enable), .DP_Shift(Controller_1_dp_shift),
    .Carry(Controller_1_carry), .RAM_Addr(RAM_Addr), .Load(Controller_1_load), .Store(Store), .Clk(Clk),
    .Reset(Reset));  // open: PC
  assign bit_extender_1_out = {{31{Controller_1_imm32_enable}}, Controller_1_imm32_enable};  // Bit_Extender bit_extender_1
  assign bit_extender_2_out = {{4{Controller_1_dp_shift}}, Controller_1_dp_shift};  // Bit_Extender bit_extender_2
  assign and_1_out = bit_extender_1_out & Controller_1_imm32;  // AND_Gate and_1, 32 bits wide
  assign and_2_out = bit_extender_2_out & Controller_1_imm5;  // AND_Gate and_2, 5 bits wide
  assign and_3_out = ~bit_extender_2_out & AOut[4:0];  // AND_Gate and_3, 5 bits wide
  assign bit_extender_3_out = {{31{Controller_1_load}}, Controller_1_load};  // Bit_Extender bit_extender_3
  assign and_4_out = RAM_In & bit_extender_3_out;  // AND_Gate and_4, 32 bits wide
  assign or_1_out = and_2_out | and_3_out;  // OR_Gate or_1, 5 bits wide
  assign or_2_out = resultat_1_s | and_4_out | and_1_out;  // OR_Gate or_2, 32 bits wide
  BancRegistre Regs_1 (
    .Clk(Clk), .Reset(Reset), .DataIn(or_2_out), .RegB(Controller_1_rn), .BOut(Regs_1_bout), .AOut(AOut),
    .RegA(Controller_1_rm), .RegDest(Controller_1_rd), .R0(R0), .R1(R1), .R2(R2), .R3(R3), .R4(R4), .R5(R5),
    .R6(R6), .R7(R7));
  Resultat resultat_1 (
    .S(resultat_1_s), .Flags(resultat_1_flags), .in_2(Controller_1_carry), .in_3(or_1_out), .in_4(AOut),
    .in_5(Regs_1_bout), .in_1(Controller_1_alu_opcode));
  assign bit_extender_4_out = {{31{Store}}, Store};  // Bit_Extender bit_extender_4
  assign RAM_Out = AOut & bit_extender_4_out;  // AND_Gate and_5, 32 bits wide
endmodule
