// Logisim project tmpFlags_APSR.circ as structural Verilog
module BancRegistre (
  input  [31:0] DataIn,
  input  [2:0] RegA,
  input  Clk,
  input  Reset,
  input  [2:0] RegDest,
  input  [2:0] RegB,
  output [31:0] AOut,
  output [31:0] R0,
  output [31:0] R1,
  output [31:0] R2,
  output [31:0] R3,
  output [31:0] R4,
  output [31:0] R5,
  output [31:0] R6,
  output [31:0] R7,
  output [31:0] BOut
);

  wire demultiplexer_1_out0, demultiplexer_1_out1, demultiplexer_1_out2, demultiplexer_1_out3,
       demultiplexer_1_out4, demultiplexer_1_out5, demultiplexer_1_out6, demultiplexer_1_out7;
  wire [31:0] register_1_q, register_2_q, register_3_q, register_4_q, register_5_q, register_6_q,
       register_7_q, register_8_q;

  Demultiplexer #(.select(3), .enable("false")) demultiplexer_1 (
    .out0(demultiplexer_1_out0), .out1(demultiplexer_1_out1), .out2(demultiplexer_1_out2),
    .out3(demultiplexer_1_out3), .out4(demultiplexer_1_out4), .out5(demultiplexer_1_out5),
    .out6(demultiplexer_1_out6), .out7(demultiplexer_1_out7), .sel(RegDest));  // open: in
  Register #(.width(32)) register_1 (.D(DataIn), .en(demultiplexer_1_out0), .clk(Clk), .Q(register_1_q), .clr(Reset));
  Register #(.width(32)) register_2 (.D(DataIn), .en(demultiplexer_1_out1), .clk(Clk), .Q(register_2_q), .clr(Reset));
  Register #(.width(32)) register_3 (.D(DataIn), .en(demultiplexer_1_out2), .clk(Clk), .Q(register_3_q), .clr(Reset));
  Register #(.width(32)) register_4 (.D(DataIn), .en(demultiplexer_1_out3), .clk(Clk), .Q(register_4_q));  // open: clr
  Register #(.width(32)) register_5 (.D(DataIn), .en(demultiplexer_1_out4), .clk(Clk), .Q(register_5_q), .clr(Reset));
  Register #(.width(32)) register_6 (.D(DataIn), .en(demultiplexer_1_out5), .clk(Clk), .Q(register_6_q), .clr(Reset));
  Register #(.width(32)) register_7 (.D(DataIn), .en(demultiplexer_1_out6), .clk(Clk), .Q(register_7_q), .clr(Reset));
  Register #(.width(32)) register_8 (.D(DataIn), .en(demultiplexer_1_out7), .clk(Clk), .Q(register_8_q), .clr(Reset));
  Multiplexer #(.select(3), .width(32), .enable("false")) multiplexer_1 (
    .in0(register_1_q), .in1(register_2_q), .in2(register_3_q), .in3(register_4_q), .in4(register_5_q),
    .in5(register_6_q), .in6(register_7_q), .in7(register_8_q), .out(AOut), .sel(RegA));
  Multiplexer #(.select(3), .width(32), .enable("false")) multiplexer_2 (
    .in0(register_1_q), .in1(register_2_q), .in2(register_3_q), .in3(register_4_q), .in4(register_5_q),
    .in5(register_6_q), .in6(register_7_q), .in7(register_8_q), .out(BOut), .sel(RegB));
endmodule

module Resultat (
  input  [3:0] in_1,
  input  in_2,
  input  [4:0] in_3,
  input  [31:0] in_4,
  input  [31:0] in_5,
  output [31:0] S,
  output [3:0] Flags
);

  // Probe on in_1
  ALU alu_1 (.Codop(in_1), .A(in_4), .Shift(in_3), .CarryIn(in_2), .B(in_5), .S(S), .Flags(Flags));
endmodule

module Operations (
  input  [4:0] Shift,
  input  CarryIn,
  input  [31:0] A,
  input  [31:0] B,
  output [31:0] ORR,
  output [31:0] TST,
  output [31:0] MUL,
  output [31:0] EOR,
  output [31:0] MULCout,
  output [31:0] LSL,
  output [31:0] lAND,
  output [31:0] ADC,
  output ADCCout,
  output [31:0] ASR,
  output [31:0] LSR,
  output [31:0] BIC,
  output [31:0] RSB,
  output [31:0] lROR,
  output [31:0] CMP,
  output [31:0] MVN,
  output CMPCout,
  output [31:0] SBC,
  output [31:0] CMN,
  output CMNCout,
  output SBCOut,
  output CMNV
);

  wire ANeg, APos, BNeg, BPos, comparator_1_gt, comparator_1_lt, negator_2_out;

  Subtractor #(.width(32)) subtractor_1 (.a(A), .b(B), .out(CMP), .bout(CMPCout));  // open: bin
  assign EOR = A ^ B;  // XOR_Gate xor_1, 32 bits wide
  Shifter #(.width(32)) shifter_1 (.in(B), .\dist (Shift), .out(LSL));
  Shifter #(.width(32), .shift("ar")) shifter_2 (.in(B), .\dist (Shift), .out(ASR));
  Negator #(.width(32)) negator_1 (.in(B), .out(RSB));
  Adder #(.width(32)) adder_1 (.a(A), .b(B), .out(CMN), .cout(CMNCout));  // open: cin
  Comparator #(.width(32)) comparator_1 (
    .a(CMN), .b({32{1'b0}}), .gt(comparator_1_gt), .lt(comparator_1_lt));  // open: eq
  and and_1 (CMNV, ANeg, BNeg, comparator_1_gt);
  and and_2 (CMNV, comparator_1_lt, APos, BPos);
  assign lAND = A & B;  // AND_Gate and_3, 32 bits wide
  assign MVN = ~B;  // NOT_Gate not_1, 32 bits wide
  assign ORR = A | B;  // OR_Gate or_1, 32 bits wide
  Multiplier #(.width(32)) multiplier_1 (.a(A), .b(B), .out(MUL), .cout(MULCout));  // open: cin
  assign BIC = A & MVN;  // AND_Gate and_4, 32 bits wide
  Negator #(.width(1)) negator_2 (.in(CarryIn), .out(negator_2_out));
  Subtractor #(.width(32)) subtractor_2 (.a(A), .b(B), .out(SBC), .bin(negator_2_out), .bout(SBCOut));
  Adder #(.width(32)) adder_2 (.a(A), .b(B), .out(ADC), .cin(CarryIn), .cout(ADCCout));
  Comparator #(.width(32)) comparator_2 (.a(A), .b({32{1'b0}}), .gt(APos), .lt(ANeg));  // open: eq
  Comparator #(.width(32)) comparator_3 (.a(B), .b({32{1'b0}}), .gt(BPos), .lt(BNeg));  // open: eq
  Shifter #(.width(32), .shift("ar")) shifter_3 (.in(B), .\dist (Shift), .out(LSR));
  Shifter #(.width(32), .shift("rr")) shifter_4 (.in(B), .\dist (Shift), .out(lROR));

  assign TST = EOR;

  // Other names for the same wires on the sheet: Cin = CarryIn
endmodule

module ALU (
  input  [3:0] Codop,
  input  [31:0] A,
  input  [4:0] Shift,
  input  CarryIn,
  input  [31:0] B,
  output [31:0] S,
  output [3:0] Flags
);

  wire ADCCout, and_1_out, and_2_out, bitselector_1_out, bitselector_3_out, bitselector_4_out,
       bitselector_5_out, bitselector_6_out, CMNCout, CMPCout, not_1_out, SBCout, subtractor_1_bout,
       undriven, xor_1_out, xor_2_out;
  wire [4:0] negator_1_out, subtractor_1_out;
  wire [31:0] ADC, ASR, BIC, CMN, CMP, EOR, lAND, lROR, LSL, LSR, MUL, MULCout, MVN, ORR, RSB, SBC, TST;

  Multiplexer #(.select(4), .width(32), .enable("false")) multiplexer_1 (
    .in0(lAND), .in1(EOR), .in2(LSL), .in3(LSR), .in4(ASR), .in5(ADC), .in6(SBC), .in7(lROR), .in8(TST),
    .in9(RSB), .in10(CMP), .in11(CMN), .in12(ORR), .in13(MUL), .in14(BIC), .in15(MVN), .out(S), .sel(Codop));
  Comparator #(.width(32)) comparator_1 (.a(S), .b({32{1'b0}}), .eq(Flags[1]), .lt(Flags[0]));  // open: gt
  Operations operations_1 (
    .Shift(Shift), .CarryIn(CarryIn), .A(A), .B(B), .ORR(ORR), .TST(TST), .MUL(MUL), .EOR(EOR),
    .MULCout(MULCout), .LSL(LSL), .lAND(lAND), .ADC(ADC), .ADCCout(ADCCout), .ASR(ASR), .LSR(LSR), .BIC(BIC),
    .RSB(RSB), .lROR(lROR), .CMP(CMP), .MVN(MVN), .CMPCout(CMPCout), .SBC(SBC), .CMN(CMN), .CMNCout(CMNCout),
    .SBCOut(SBCout));  // open: CMNV
  Negator #(.width(5)) negator_1 (.in(Shift), .out(negator_1_out));
  Subtractor #(.width(5)) subtractor_1 (
    .a(Shift), .b(5'b00001), .out(subtractor_1_out), .bout(subtractor_1_bout));  // open: bin
  BitSelector #(.width(32)) bitselector_1 (.in(A), .out(bitselector_1_out), .sel({5{1'b1}}));
  BitSelector #(.width(32)) bitselector_2 (.in(A), .out(bitselector_1_out), .sel({5{1'b1}}));
  BitSelector #(.width(32)) bitselector_3 (.in(B), .out(bitselector_3_out), .sel({5{1'b1}}));
  BitSelector #(.width(32)) bitselector_4 (.in(S), .out(bitselector_4_out), .sel({5{1'b1}}));
  BitSelector #(.width(32)) bitselector_5 (.in(B), .out(bitselector_5_out), .sel(negator_1_out));
  BitSelector #(.width(32)) bitselector_6 (.in(B), .out(bitselector_6_out), .sel(subtractor_1_out));
  xor xor_1 (xor_1_out, bitselector_1_out, bitselector_3_out);
  xor xor_2 (xor_2_out, bitselector_1_out, bitselector_4_out);
  Multiplexer #(.select(4), .enable("false")) multiplexer_2 (
    .in0(1'b0), .in1(1'b0), .in2(bitselector_5_out), .in3(bitselector_6_out), .in4(bitselector_6_out),
    .in5(ADCCout), .in6(SBCout), .in7(undriven), .in8(1'b0), .in9(1'b1), .in10(CMPCout), .in11(CMNCout),
    .in12(1'b0), .in13(1'b0), .in14(1'b0), .in15(1'b0), .out(Flags[2]), .sel(Codop));
  not not_1 (not_1_out, xor_1_out);
  and and_1 (and_1_out, not_1_out, xor_2_out);
  and and_2 (and_2_out, xor_1_out, xor_2_out);
  Multiplexer #(.select(4), .enable("false")) multiplexer_3 (
    .in0(1'b0), .in1(1'b0), .in2(1'b0), .in3(1'b0), .in4(1'b0), .in5(and_1_out), .in6(and_2_out), .in7(1'b0),
    .in8(1'b0), .in9(1'b0), .in10(and_2_out), .in11(and_1_out), .in12(1'b0), .in13(1'b0), .in14(1'b0),
    .in15(1'b0), .out(Flags[3]), .sel(Codop));

  // Other names for the same wires on the sheet: N = Flags[0]; Z = Flags[1]; C = Flags[2]; V = Flags[3]

  // Notes on the sheet:
  //   Note: for ROR, C = N
  //   Note 2: assume that shift > 0 for LSL and LSR
endmodule

module tmp (
);

  wire and_1_out, and_2_out, and_3_out, and_4_out, bitselector_1_out, bitselector_2_out, bitselector_3_out,
       bitselector_5_out, bitselector_6_out, bitselector_7_out, not_1_out, V, xnor_1_out, xor_1_out,
       xor_2_out, xor_3_out, xor_4_out, xor_5_out;
  wire [3:0] Codop;
  wire [31:0] A, B, S;

  BitSelector #(.width(32)) bitselector_1 (.in(B), .out(bitselector_1_out), .sel({5{1'b1}}));
  BitSelector #(.width(32)) bitselector_2 (.in(S), .out(bitselector_2_out), .sel({5{1'b1}}));
  BitSelector #(.width(32)) bitselector_3 (.in(A), .out(bitselector_3_out), .sel({5{1'b1}}));
  BitSelector #(.width(32)) bitselector_4 (.in(A), .out(bitselector_3_out), .sel({5{1'b1}}));
  BitSelector #(.width(32)) bitselector_5 (.in(B), .out(bitselector_5_out), .sel({5{1'b1}}));
  BitSelector #(.width(32)) bitselector_6 (.in(S), .out(bitselector_6_out), .sel({5{1'b1}}));
  BitSelector #(.width(32)) bitselector_7 (.in(A), .out(bitselector_7_out), .sel({5{1'b1}}));
  BitSelector #(.width(32)) bitselector_8 (.in(A), .out(bitselector_7_out), .sel({5{1'b1}}));
  xor xor_1 (xor_1_out, bitselector_7_out, bitselector_1_out);
  xor xor_2 (xor_2_out, bitselector_1_out, bitselector_2_out);
  xnor xnor_1 (xnor_1_out, bitselector_3_out, bitselector_5_out);
  xor xor_3 (xor_3_out, bitselector_3_out, bitselector_5_out);
  xor xor_4 (xor_4_out, bitselector_3_out, bitselector_6_out);
  not not_1 (not_1_out, xor_2_out);
  xor xor_5 (xor_5_out, bitselector_3_out, bitselector_6_out);
  and and_1 (and_1_out, xor_1_out, not_1_out);
  and and_2 (and_2_out, xor_1_out, xor_2_out);
  and and_3 (and_3_out, xnor_1_out, xor_5_out);
  and and_4 (and_4_out, xor_3_out, xor_4_out);
  Multiplexer #(.select(4), .enable("false")) multiplexer_1 (
    .in0(1'b0), .in1(1'b0), .in2(1'b0), .in3(1'b0), .in4(1'b0), .in5(and_1_out), .in6(and_2_out), .in7(1'b0),
    .in8(1'b0), .in9(1'b0), .in10(and_2_out), .in11(and_1_out), .in12(1'b0), .in13(1'b0), .in14(1'b0),
    .in15(1'b0), .out(V), .sel(Codop));
  Multiplexer #(.select(4), .enable("false")) multiplexer_2 (
    .in0(1'b0), .in1(1'b0), .in2(1'b0), .in3(1'b0), .in4(1'b0), .in5(and_3_out), .in6(and_4_out), .in7(1'b0),
    .in8(1'b0), .in9(1'b0), .in10(and_4_out), .in11(and_3_out), .in12(1'b0), .in13(1'b0), .in14(1'b0),
    .in15(1'b0), .out(V), .sel(Codop));
endmodule

module Controller (
  input  [15:0] Inst,
  input  [3:0] Flags,
  input  Clk,
  input  Reset,
  output Carry,
  output DP_Shift,
  output Imm32_Enable,
  output [4:0] Imm5,
  output [31:0] Imm32,
  output [3:0] ALU_Opcode,
  output [2:0] Rm,
  output [2:0] Rn,
  output [2:0] Rd,
  output [31:0] RAM_Addr,
  output Load,
  output Store,
  output [7:0] PC
);

  wire Conditional_1_verified, Load_Store_1_pc_hold, not_1_out, Opcode_Decoder_1_conditional,
       Opcode_Decoder_1_data_processing, Opcode_Decoder_1_load_store, Opcode_Decoder_1_shift,
       Opcode_Decoder_1_sp_address, Shift_Add_Sub_Mov_1_p3, SP_Address_1_write_enable;
  wire [2:0] Data_Processing_1_p4, Data_Processing_1_p5, Data_Processing_1_p6, Load_Store_1_rd,
       Load_Store_1_rm, Shift_Add_Sub_Mov_1_p8, Shift_Add_Sub_Mov_1_p9, Shift_Add_Sub_Mov_1_p10;
  wire [3:0] Data_Processing_1_p3, flags_apsr_1_flags_out, or_1_out, Shift_Add_Sub_Mov_1_p7,
       Shift_Add_Sub_Mov_1_p11, undriven;
  wire [7:0] adder_1_out, adder_2_out, Conditional_1_offset;
  wire [31:0] SP_Address_1_new_stack_pointer, Stack_Pointer_q;

  Register #(.width(32)) Stack_Pointer (
    .D(SP_Address_1_new_stack_pointer), .en(SP_Address_1_write_enable), .clk(Clk), .Q(Stack_Pointer_q),
    .clr(Reset));
  Opcode_Decoder Opcode_Decoder_1 (
    .Opcode(Inst[15:10]), .Shift(Opcode_Decoder_1_shift), .Data_Processing(Opcode_Decoder_1_data_processing),
    .Load_Store(Opcode_Decoder_1_load_store), .SP_Address(Opcode_Decoder_1_sp_address),
    .Conditional(Opcode_Decoder_1_conditional));
  assign or_1_out = undriven | Shift_Add_Sub_Mov_1_p11;  // OR_Gate or_1, 4 bits wide
  // Shift_Add_Sub_Mov Shift_Add_Sub_Mov_1: pin names not known; wires that end beside it: Inst, Opcode_Decoder_1_shift, Shift_Add_Sub_Mov_1_p3, Imm32_Enable, Imm5, Imm32, Shift_Add_Sub_Mov_1_p7, Shift_Add_Sub_Mov_1_p8, Shift_Add_Sub_Mov_1_p9, Shift_Add_Sub_Mov_1_p10, Shift_Add_Sub_Mov_1_p11
  // Data_Processing Data_Processing_1: pin names not known; wires that end beside it: Inst, Opcode_Decoder_1_data_processing, Data_Processing_1_p3, Data_Processing_1_p4, Data_Processing_1_p5, Data_Processing_1_p6
  Flags_APSR flags_apsr_1 (
    .Update_Mask(or_1_out), .Flags_In(Flags), .Clk(Clk), .Rst(Reset), .Flags_Out(flags_apsr_1_flags_out));
  Load_Store Load_Store_1 (
    .Rm(Load_Store_1_rm), .Instruction(Inst), .Rd(Load_Store_1_rd), .Load(Load),
    .Enable(Opcode_Decoder_1_load_store), .RAM_Addr(RAM_Addr), .Stack_Pointer(Stack_Pointer_q),
    .Store(Store), .Clk(Clk), .Reset(Reset), .PC_Hold(Load_Store_1_pc_hold));
  Conditional Conditional_1 (
    .Instruction(Inst), .Verified(Conditional_1_verified), .Enable(Opcode_Decoder_1_conditional),
    .Offset(Conditional_1_offset), .Z(flags_apsr_1_flags_out[2]), .V(flags_apsr_1_flags_out[0]),
    .N(flags_apsr_1_flags_out[3]), .C(flags_apsr_1_flags_out[1]));
  SP_Address SP_Address_1 (
    .New_Stack_Pointer(SP_Address_1_new_stack_pointer), .Stack_Pointer(Stack_Pointer_q),
    .Enable(Opcode_Decoder_1_sp_address), .Instruction(Inst), .Write_Enable(SP_Address_1_write_enable));
  Adder adder_1 (.a(8'h3), .b(Conditional_1_offset), .out(adder_1_out), .cin(1'b0));  // open: cout
  Adder adder_2 (.a(adder_1_out), .b(PC), .out(adder_2_out), .cin(1'b0));  // open: cout
  and and_1 (DP_Shift, Opcode_Decoder_1_shift, ~Opcode_Decoder_1_data_processing);  // AND_Gate
  not not_1 (not_1_out, Load_Store_1_pc_hold);
  Counter counter_1 (
    .clr(Reset), .load(Conditional_1_verified), .up(1'b1), .count(not_1_out), .clk(Clk), .D(adder_2_out),
    .Q(PC));  // open: carry
  Multiplexer #(.enable("false")) multiplexer_1 (
    .in0(flags_apsr_1_flags_out[1]), .in1(Shift_Add_Sub_Mov_1_p3), .out(Carry), .sel(DP_Shift));
  assign ALU_Opcode = Shift_Add_Sub_Mov_1_p7 | Data_Processing_1_p3;  // OR_Gate or_2, 4 bits wide
  assign Rm = Shift_Add_Sub_Mov_1_p8 | Data_Processing_1_p4 | Load_Store_1_rm;  // OR_Gate or_3, 3 bits wide
  assign Rn = Shift_Add_Sub_Mov_1_p9 | Data_Processing_1_p5;  // OR_Gate or_4, 3 bits wide
  assign Rd = Shift_Add_Sub_Mov_1_p10 | Data_Processing_1_p6 | Load_Store_1_rd;  // OR_Gate or_5, 3 bits wide

  // Notes on the sheet:
  //   Extract carry
  //   Extract Opcode
  //   IF Reg_Imm=1 THEN use shift value from register ELSE use shift value from Imm5
  //   Buffer flags for next instruction
  //   Add 3 to offset because ARM pre-increments PC
  //   and does an additionnal prefect operation
endmodule

module Conditional (
  input  Enable,
  input  [15:0] Instruction,
  input  N,
  input  Z,
  input  C,
  input  V,
  output [7:0] Offset,
  output Verified
);
endmodule

module Opcode_Decoder (
  input  [5:0] Opcode,
  output Shift,
  output Data_Processing,
  output Load_Store,
  output SP_Address,
  output Conditional
);


  // Notes on the sheet:
  //   Load/Store
  //   SP Address
  //   Shift, add, sub, mov
  //   Data Processing
  //   Conditional branch
endmodule

module Data_Processing (
  input  [15:0] in_1,
  input  in_2,
  output [2:0] out_3,
  output [2:0] out_4,
  output [2:0] out_5,
  output [3:0] out_6,
  output [3:0] out_7
);

  wire [3:0] bit_extender_1_out, multiplexer_1_out;

  assign bit_extender_1_out = {{3{in_2}}, in_2};  // Bit_Extender bit_extender_1
  Multiplexer #(.select(4), .width(4), .enable("false")) multiplexer_1 (
    .in0(4'b1110), .in1(4'b1110), .in2(4'b1110), .in3(4'b1110), .in4(4'b1110), .in5(4'b1111), .in6(4'b1111),
    .in7(4'b1110), .in8(4'b1110), .in9(4'b1111), .in10(4'b1111), .in11(4'b1111), .in12(4'b1110),
    .in13(4'b1100), .in14(4'b1110), .in15(4'b1110), .out(multiplexer_1_out), .sel(in_1[9:6]));
  assign out_6 = multiplexer_1_out & bit_extender_1_out;  // AND_Gate and_1, 4 bits wide

  assign out_3 = in_1[2:0];
  assign out_4 = in_1[2:0];
  assign out_5 = in_1[5:3];
  assign out_7 = in_1[9:6];

  // Other names for the same wires on the sheet: RdRn[2:0] = in_1[2:0]; Rm[2:0] = in_1[5:3]; Codop[3:0] = in_1[9:6]

  // Notes on the sheet:
  //   Note 2: RSB instruction has Rn as 1st operand.
  //   MUL instruction has Rn as 1st operand and Rdm as 2nd operand
  //   For simplification purposes, Rm is used for 1st operand both here and in the ALU.
  //   Pull output low on Enable = 0
  //   Note: instructions that does not save the result will still have the second operand as the destination register, the ALU will copy the second register to the destination register
endmodule

module Shift_Add_Sub_Mov (
  input  [15:0] Instruction,
  input  Enable,
  output [3:0] ALU_Opcode,
  output [3:0] Flags_Update_Mask,
  output Carry,
  output Imm32_Enable,
  output [31:0] Imm32,
  output [2:0] Rd,
  output [2:0] Rm,
  output [2:0] Rn,
  output [4:0] Imm5,
  output [2:0] imm3,
  output [7:0] imm8
);

  wire and_1_out, and_2_out, and_3_out, and_4_out, and_5_out, and_6_out, and_7_out, and_8_out,
       priority_encoder_1_en_out;
  wire [2:0] priority_encoder_1_out;

  // Probe on Instruction[13]
  Multiplexer #(.select(3), .width(3), .enable("false")) multiplexer_1 (
    .in0(Instruction[2:0]), .in1(Instruction[2:0]), .in2(Instruction[2:0]), .in3(Instruction[2:0]),
    .in4(Instruction[2:0]), .in5(Instruction[2:0]), .in6(Instruction[2:0]), .in7(Instruction[2:0]), .out(Rd),
    .sel(priority_encoder_1_out));
  // Probe on Instruction[5:3]
  and and_1 (and_1_out, ~Instruction[13], ~Instruction[12], ~Instruction[11]);  // AND_Gate
  and and_2 (and_2_out, ~Instruction[13], ~Instruction[12], Instruction[11]);  // AND_Gate
  and and_3 (and_3_out, ~Instruction[13], Instruction[12], ~Instruction[11]);  // AND_Gate
  and and_4 (and_4_out, ~Instruction[13], Instruction[12], Instruction[11], ~Instruction[10], ~Instruction[9]);  // AND_Gate
  and and_5 (and_5_out, ~Instruction[13], Instruction[12], Instruction[11], ~Instruction[10], Instruction[9]);  // AND_Gate
  and and_6 (and_6_out, ~Instruction[13], Instruction[12], Instruction[11], Instruction[10], ~Instruction[9]);  // AND_Gate
  and and_7 (and_7_out, ~Instruction[13], Instruction[12], Instruction[11], Instruction[10], Instruction[9]);  // AND_Gate
  and and_8 (and_8_out, Instruction[13], ~Instruction[12], ~Instruction[11]);  // AND_Gate
  // Probe on and_1_out
  // Probe on priority_encoder_1_en_out
  Priority_Encoder priority_encoder_1 (
    .in0(and_1_out), .in1(and_2_out), .in2(and_3_out), .in3(and_4_out), .in4(and_5_out), .in5(and_6_out),
    .in6(and_7_out), .in7(and_8_out), .out(priority_encoder_1_out), .en_in(1'b1),
    .en_out(priority_encoder_1_en_out));  // open: gs
  // Probe on priority_encoder_1_out
  Multiplexer #(.select(3), .width(4), .enable("false")) multiplexer_2 (
    .in0(4'b0010), .in1(4'b0011), .in2(4'b0100), .in3(4'b0000), .in4(4'b0000), .in5(4'b0000), .in6(4'b0000),
    .in7(4'b0000), .out(ALU_Opcode), .sel(priority_encoder_1_out));
  Multiplexer #(.select(3), .width(3), .enable("false")) multiplexer_3 (
    .in0(Instruction[5:3]), .in1(Instruction[5:3]), .in2(Instruction[5:3]), .in3(Instruction[8:6]),
    .in4(Instruction[8:6]), .in5(3'b000), .in6(3'b000), .in7(3'b000), .out(Rm), .sel(priority_encoder_1_out));
  Multiplexer #(.select(3), .width(4), .enable("false")) multiplexer_4 (
    .in0(4'b1110), .in1(4'b1110), .in2(4'b1110), .in3(4'b1111), .in4(4'b1111), .in5(4'b1111), .in6(4'b1111),
    .in7(4'b1100), .out(Flags_Update_Mask), .sel(priority_encoder_1_out));
  Multiplexer #(.select(3), .width(3), .enable("false")) multiplexer_5 (
    .in0(3'b000), .in1(3'b000), .in2(3'b000), .in3(Instruction[5:3]), .in4(Instruction[5:3]),
    .in5(Instruction[5:3]), .in6(Instruction[5:3]), .in7(3'b000), .out(Rn), .sel(priority_encoder_1_out));
  Multiplexer #(.select(3), .width(5), .enable("false")) multiplexer_6 (
    .in0(Instruction[10:6]), .in1(Instruction[10:6]), .in2(Instruction[10:6]), .in3({5{1'b0}}),
    .in4({5{1'b0}}), .in5({5{1'b0}}), .in6({5{1'b0}}), .in7({5{1'b0}}), .out(Imm5),
    .sel(priority_encoder_1_out));
  Multiplexer #(.select(3), .width(3), .enable("false")) multiplexer_7 (
    .in0(3'b000), .in1(3'b000), .in2(3'b000), .in3(Instruction[8:6]), .in4(Instruction[8:6]), .in5(3'b000),
    .in6(3'b000), .in7(3'b000), .out(imm3), .sel(priority_encoder_1_out));
  Multiplexer #(.select(3), .width(8), .enable("false")) multiplexer_8 (
    .in0({8{1'b0}}), .in1({8{1'b0}}), .in2({8{1'b0}}), .in3({8{1'b0}}), .in4({8{1'b0}}), .in5({8{1'b0}}),
    .in6({8{1'b0}}), .in7(Instruction[7:0]), .out(imm8), .sel(priority_encoder_1_out));

  // Notes on the sheet:
  //   Pull output low on Enable = 0
  //   Note 3: Imm32_Enable forces the use of the immediate for Rm register
  //   Note: ALU uses Rn register for shifts. Use Rn instead of Rm for shifts (immediate) here too
  //   Note 2: MOV uses RSB ALU opcode with Imm8 reversed so that it is copied to output register
  //   LSL
  //   LSR
  //   ASR
  //   ADD(register)
  //   SUB (register)
  //   ADD (immediate)
  //   SUB (immediate)
  //   MOV (immediate)
  //   Enable carry for SUB since it is reversed in ALU
  //   ALU will use Imm32 instead of Rm
endmodule

module Load_Store (
  input  [15:0] Instruction,
  input  Enable,
  input  [31:0] Stack_Pointer,
  input  Clk,
  input  Reset,
  output Store,
  output Load,
  output PC_Hold,
  output [2:0] Rm,
  output [2:0] Rd,
  output [31:0] RAM_Addr
);


  // Notes on the sheet:
  //   Delay load and hold PC for 1 cycle for the RAM to send out requested data 
endmodule

module SP_Address (
  input  Enable,
  input  [15:0] Instruction,
  input  [31:0] Stack_Pointer,
  output Write_Enable,
  output [31:0] New_Stack_Pointer
);


  // Notes on the sheet:
  //   Pull output low on Enable = 0
endmodule

module Flags_APSR (
  input  [3:0] Update_Mask,
  input  [3:0] Flags_In,
  input  Clk,
  input  Rst,
  output [3:0] Flags_Out
);

  wire [3:0] and_1_out, and_2_out, not_1_out, or_1_out;

  assign and_1_out = Flags_Out & not_1_out;  // AND_Gate and_1, 4 bits wide
  assign not_1_out = ~Update_Mask;  // NOT_Gate not_1, 4 bits wide
  assign and_2_out = Update_Mask & Flags_In;  // AND_Gate and_2, 4 bits wide
  assign or_1_out = and_1_out | and_2_out;  // OR_Gate or_1, 4 bits wide
  Register #(.width(4)) register_1 (.D(or_1_out), .en(1'b1), .clk(Clk), .Q(Flags_Out), .clr(Rst));
endmodule

module CPU (
  input  [31:0] RAM_In,
  input  [15:0] ROM_In,
  input  Clk,
  input  Reset,
  output [7:0] ROM_Addr,
  output [31:0] R3,
  output [31:0] R7,
  output [31:0] R2,
  output [31:0] R6,
  output [31:0] RAM_Addr,
  output [31:0] R1,
  output [31:0] R5,
  output [31:0] R0,
  output [31:0] R4,
  output [31:0] RAM_Out,
  output Store
);

  // Controller_Controller Controller_1: pin names not known
  BancDeRegistres_BancRegistre Regs_1 (
    .R0(R0), .R1(R1), .R2(R2), .R3(R3), .R4(R4), .R5(R5), .R6(R6), .R7(R7));  // open: Clk, Reset, DataIn, RegB, BOut, AOut, RegA, RegDest
endmodule
